# Fritzing sketch Arduino-Uno-GesamteVerdrahtung (saved by Fritzing 1.0.2b)
breadboards: 1

parts:
  Bauteil1 = Arduino Uno (Rev3) - ICSP
  S4 = Pushbutton [package="[SMD]"]
  R4 = Resistor [tolerance=±5% power=0.25W resistance=10k package=THT]
  LED1 = smd LED [color="Red (633nm)" package="1206 [SMD]"]
  R5 = Resistor [tolerance=±5% power=0.25W resistance=220 package=THT]
  R6 = Rotary Potentiometer (Large) [maximum_resistance=10kΩ knob_status=50% power=0.5W package=THT]
  Bauteil2 = BH1750

nets:
  N1: Bauteil1.A2, R6.wiper
  N2: Bauteil1.A4/SDA, Bauteil2.SDA
  N3: Bauteil1.A5/SCL, Bauteil2.SCL
  N4: Bauteil1.D5_PWM, R5.Pin_0
  N5: Bauteil1.D6_PWM, S4.Pin_1, S4.Pin_2, R4.Pin_0
  3V3: Bauteil1.3V3, S4.Pin_3, S4.Pin_4, R4.Pin_1, R6.leg1, Bauteil2.VCC
  GND: Bauteil1.GND, LED1.cathode, R6.leg2, Bauteil2.GND
  N6: LED1.anode, R5.Pin_1

notes:
  GPIOs werden im Kurs oft exemplarisch genutzt und je nach Bedarf zur Veranschaulichung angepasst.

custom parts:
  BH1750: Light Sensor
